// Logisim project EveryThing.circ as structural Verilog: 1 circuit, main circuit main
module main (
  input  in_1,
  input  in_2,
  input  in_3,
  input  SR_Flip_Flop,
  input  in_5,
  input  [15:0] in_6,
  input  in_7,
  input  in_8,
  input  in_9,
  input  in_10,
  input  in_11,
  input  in_12,
  input  [2:0] in_13,
  input  in_14,
  input  Data_Flip_Flop,
  input  in_16,
  input  Full_Adder,
  input  in_18,
  input  in_19,
  input  in_20,
  input  in_21,
  input  in_22,
  input  in_23,
  input  in_24,
  input  in_25,
  input  [1:0] _2_bit_Adder,
  input  [1:0] in_27,
  input  [15:0] in_28,
  input  in_29,
  input  in_30,
  input  DeMux,
  input  [3:0] _4_bit_Adder,
  input  [3:0] in_33,
  input  [15:0] in_34,
  input  in_35,
  input  in_36,
  input  [15:0] in_37,
  input  in_38,
  input  [15:0] in_39,
  input  [15:0] in_40,
  input  in_41,
  input  in_42,
  input  [5:0] in_43,
  input  [15:0] in_44,
  input  [15:0] in_45,
  input  in_46,
  input  in_47,
  input  [15:0] in_48,
  input  in_49,
  input  in_50,
  input  in_51,
  input  in_52,
  input  [15:0] in_53,
  input  [15:0] in_54,
  input  in_55,
  input  in_56,
  input  in_57
);

  wire adder_3_cout, adder_4_cout, adder_5_cout, adder_5_out, adder_6_cout, adder_7_cout, and_1_out,
       and_2_out, and_3_out, and_4_out, and_5_out, and_6_out, and_7_out, clock_1_out, clock_2_out,
       clock_3_out, clock_4_out, clock_5_out, clock_6_out, clock_7_out, d_ff_1_q, demultiplexer_2_out0,
       demultiplexer_2_out1, demultiplexer_5_out0, demultiplexer_5_out1, demultiplexer_5_out2,
       demultiplexer_5_out3, demultiplexer_5_out4, demultiplexer_5_out5, demultiplexer_5_out6,
       demultiplexer_5_out7, demultiplexer_6_out0, demultiplexer_6_out1, demultiplexer_6_out2,
       demultiplexer_6_out3, demultiplexer_6_out4, demultiplexer_6_out5, demultiplexer_6_out6,
       demultiplexer_6_out7, ledbar_10_p2, multiplexer_1_out, multiplexer_12_out, nand_1_out, nand_2_out,
       nand_3_out, nand_4_out, nand_5_out, nand_6_out, nand_7_out, nand_8_out, nand_9_out, nand_10_out,
       nand_11_out, nand_12_out, nand_13_out, nand_14_out, nand_15_out, nand_16_out, nand_17_out,
       nand_18_out, nand_19_out, nand_20_out, nand_21_out, nand_22_out, nand_23_out, not_1_out, not_2_out,
       not_7_out, or_2_out, or_3_out, or_4_out, or_5_out, or_6_out, or_7_out, or_8_out, or_9_out, or_10_out,
       or_11_out, or_12_out, or_13_out, or_14_out, or_15_out, or_16_out, or_17_out, or_18_out, or_19_out,
       or_20_out, or_21_out, xor_2_out, xor_3_out, xor_4_out;
  wire [1:0] adder_3_out;
  wire [3:0] adder_7_out;
  wire [15:0] adder_8_out, adder_9_out, and_8_out, demultiplexer_1_out0, demultiplexer_1_out1,
       demultiplexer_3_out0, demultiplexer_3_out1, demultiplexer_4_out0, demultiplexer_4_out1, ledbar_8_p1,
       ledbar_9_p2, ledbar_11_p1, ledbar_12_p1, multiplexer_2_out, multiplexer_3_out, multiplexer_4_out,
       multiplexer_5_out, multiplexer_6_out, multiplexer_7_out, multiplexer_8_out, multiplexer_9_out,
       multiplexer_11_out, multiplexer_13_out, multiplexer_14_out, not_4_out, not_5_out, not_6_out,
       ram_1_dout, ram_2_dout, ram_3_dout, ram_4_dout, ram_5_dout, ram_6_dout, ram_7_dout, ram_8_dout,
       register_17_q, register_18_q, register_19_q, register_20_q, register_21_q, register_22_q,
       register_23_q, register_24_q, register_25_q;

  nand nand_1 (nand_1_out, in_1, in_5);
  nand nand_2 (nand_2_out, in_7, in_7);
  nand nand_3 (nand_3_out, in_11, in_11);
  nand nand_4 (nand_4_out, in_14, in_14);
  not not_1 (not_1_out, DeMux);
  Demultiplexer #(.width(16)) demultiplexer_1 (
    .out0(demultiplexer_1_out0), .out1(demultiplexer_1_out1), .in(in_53), .sel(in_49));
  nand nand_5 (nand_5_out, nand_1_out, nand_1_out);
  LED led_1 (.in(nand_2_out));
  nand nand_6 (nand_6_out, in_19, in_19);
  nand nand_7 (nand_7_out, in_20, in_20);
  and and_1 (and_1_out, in_21, not_2_out);
  not not_2 (not_2_out, in_23);
  and and_2 (and_2_out, in_22, in_23);
  Multiplexer multiplexer_1 (.in0(in_21), .in1(in_22), .out(multiplexer_1_out), .sel(in_23));
  and and_3 (and_3_out, in_30, not_1_out);
  LED led_2 (.in(and_3_out));
  and and_4 (and_4_out, in_30, DeMux);
  LED led_3 (.in(and_4_out));
  LED led_4 (.in(demultiplexer_2_out0));
  Demultiplexer demultiplexer_2 (.out0(demultiplexer_2_out0), .out1(demultiplexer_2_out1), .in(in_30), .sel(DeMux));
  LED led_5 (.in(demultiplexer_2_out1));
  Multiplexer #(.width(16)) multiplexer_2 (.in0(in_37), .in1(in_39), .out(multiplexer_2_out), .sel(in_36));
  Multiplexer #(.width(16)) multiplexer_3 (.in0(in_40), .in1(in_45), .out(multiplexer_3_out), .sel(in_36));
  Demultiplexer #(.width(16)) demultiplexer_3 (
    .out0(demultiplexer_3_out0), .out1(demultiplexer_3_out1), .in(demultiplexer_1_out0), .sel(in_50));
  Demultiplexer #(.width(16)) demultiplexer_4 (
    .out0(demultiplexer_4_out0), .out1(demultiplexer_4_out1), .in(demultiplexer_1_out1), .sel(in_50));
  LED led_6 (.in(nand_5_out));
  // NOT_Gate not_3 is placed but not wired
  nand nand_8 (nand_8_out, nand_3_out, nand_4_out);
  LED led_7 (.in(nand_8_out));
  nand nand_9 (nand_9_out, nand_6_out, in_20);
  nand nand_10 (nand_10_out, nand_7_out, in_19);
  LED led_8 (.in(multiplexer_1_out));
  Multiplexer #(.width(16)) multiplexer_4 (
    .in0(multiplexer_2_out), .in1(multiplexer_3_out), .out(multiplexer_4_out), .sel(in_35));
  // LedBar #(.inputtype("row"), .matrixcols(16)) ledbar_1: pin names not known; wires that end beside it: multiplexer_4_out
  // LedBar #(.inputtype("row"), .matrixcols(16)) ledbar_2: pin names not known; wires that end beside it: demultiplexer_3_out0
  // LedBar #(.inputtype("row"), .matrixcols(16)) ledbar_3: pin names not known; wires that end beside it: in_50, demultiplexer_3_out1
  // LedBar #(.inputtype("row"), .matrixcols(16)) ledbar_4: pin names not known; wires that end beside it: demultiplexer_4_out0
  // LedBar #(.inputtype("row"), .matrixcols(16)) ledbar_5: pin names not known; wires that end beside it: demultiplexer_4_out1
  // OR_Gate or_1 is placed but not wired
  nand nand_11 (nand_11_out, nand_9_out, nand_9_out);
  nand nand_12 (nand_12_out, nand_10_out, nand_10_out);
  nand nand_13 (nand_13_out, nand_11_out, nand_11_out);
  nand nand_14 (nand_14_out, nand_12_out, nand_12_out);
  or or_2 (or_2_out, and_1_out, and_2_out);
  LED led_9 (.in(or_2_out));
  nand nand_15 (nand_15_out, nand_13_out, nand_14_out);
  LED led_10 (.in(nand_15_out));
  // XOR_Gate xor_1 is placed but not wired
  Adder #(.width(1)) adder_1 (
    .a(_2_bit_Adder[1]), .b(in_27[1]), .out(adder_3_out[1]), .cin(adder_3_cout));  // open: cout
  Adder #(.width(1)) adder_2 (
    .a(_4_bit_Adder[3]), .b(in_33[3]), .out(adder_7_out[3]), .cin(adder_4_cout));  // open: cout
  xor xor_2 (xor_2_out, in_2, in_3);
  and and_5 (and_5_out, in_3, in_2);
  xor xor_3 (xor_3_out, in_16, in_18);
  Adder #(.width(1)) adder_3 (
    .a(_2_bit_Adder[0]), .b(in_27[0]), .out(adder_3_out[0]), .cout(adder_3_cout));  // open: cin
  // LedBar #(.inputtype("row"), .matrixcols(2)) ledbar_6: pin names not known; wires that end beside it: adder_3_out
  Adder #(.width(1)) adder_4 (
    .a(_4_bit_Adder[2]), .b(in_33[2]), .out(adder_7_out[2]), .cin(adder_6_cout), .cout(adder_4_cout));
  Multiplexer #(.width(16)) multiplexer_5 (.in0(in_44), .in1({16{1'b0}}), .out(multiplexer_5_out), .sel(in_41));
  Multiplexer #(.width(16)) multiplexer_6 (.in0(in_48), .in1({16{1'b0}}), .out(multiplexer_6_out), .sel(in_52));
  or or_3 (or_3_out, 1'b0, ledbar_8_p1[15]);
  LED led_11 (.in(xor_2_out));
  LED led_12 (.in(and_5_out));
  Adder #(.width(1)) adder_5 (.a(in_9), .b(in_8), .out(adder_5_out), .cout(adder_5_cout));  // open: cin
  LED led_13 (.in(adder_5_out));
  LED led_14 (.in(adder_5_cout));
  and and_6 (and_6_out, xor_3_out, Full_Adder);
  and and_7 (and_7_out, in_16, in_18);
  Adder #(.width(1)) adder_6 (
    .a(_4_bit_Adder[1]), .b(in_33[1]), .out(adder_7_out[1]), .cin(adder_7_cout), .cout(adder_6_cout));
  Multiplexer #(.width(16)) multiplexer_7 (
    .in0(multiplexer_5_out), .in1(not_4_out), .out(multiplexer_7_out), .sel(in_42));
  assign not_4_out = ~multiplexer_5_out;  // NOT_Gate not_4, 16 bits wide
  Multiplexer #(.width(16)) multiplexer_8 (
    .in0(multiplexer_6_out), .in1(not_5_out), .out(multiplexer_8_out), .sel(in_51));
  assign not_5_out = ~multiplexer_6_out;  // NOT_Gate not_5, 16 bits wide
  or or_4 (or_4_out, ledbar_8_p1[15], ledbar_8_p1[14]);
  or or_5 (or_5_out, or_4_out, ledbar_8_p1[13]);
  xor xor_4 (xor_4_out, xor_3_out, Full_Adder);
  LED led_15 (.in(xor_4_out));
  or or_6 (or_6_out, and_6_out, and_7_out);
  LED led_16 (.in(or_6_out));
  Adder #(.width(1)) adder_7 (
    .a(_4_bit_Adder[0]), .b(in_33[0]), .out(adder_7_out[0]), .cout(adder_7_cout));  // open: cin
  // LedBar #(.inputtype("row"), .matrixcols(4)) ledbar_7: pin names not known; wires that end beside it: adder_7_out
  // LedBar #(.inputtype("row"), .matrixcols(16)) ledbar_8: pin names not known; wires that end beside it: ledbar_8_p1
  assign and_8_out = multiplexer_7_out & multiplexer_8_out;  // AND_Gate and_8, 16 bits wide
  Adder #(.width(16)) adder_8 (.a(multiplexer_7_out), .b(multiplexer_8_out), .out(adder_8_out));  // open: cin, cout
  or or_7 (or_7_out, or_5_out, ledbar_8_p1[12]);
  or or_8 (or_8_out, or_7_out, ledbar_8_p1[11]);
  or or_9 (or_9_out, or_8_out, ledbar_8_p1[10]);
  or or_10 (or_10_out, or_9_out, ledbar_8_p1[9]);
  Multiplexer #(.width(16)) multiplexer_9 (.in0(and_8_out), .in1(adder_8_out), .out(multiplexer_9_out), .sel(in_46));
  or or_11 (or_11_out, or_10_out, ledbar_8_p1[8]);
  or or_12 (or_12_out, ledbar_8_p1[7], or_17_out);
  or or_13 (or_13_out, or_11_out, or_12_out);
  Multiplexer #(.width(16)) multiplexer_10 (.in0(multiplexer_9_out), .in1(not_6_out), .out(ledbar_8_p1), .sel(in_47));
  assign not_6_out = ~multiplexer_9_out;  // NOT_Gate not_6, 16 bits wide
  or or_14 (or_14_out, ledbar_8_p1[3], or_19_out);
  or or_15 (or_15_out, ledbar_8_p1[4], or_14_out);
  or or_16 (or_16_out, ledbar_8_p1[5], or_15_out);
  or or_17 (or_17_out, ledbar_8_p1[6], or_16_out);
  LED led_17 (.in(or_3_out));
  LED led_18 (.in(or_13_out));
  or or_18 (or_18_out, ledbar_8_p1[1], ledbar_8_p1[0]);
  or or_19 (or_19_out, ledbar_8_p1[2], or_18_out);
  Clock clock_1 (.out(clock_1_out));
  not not_7 (not_7_out, Data_Flip_Flop);
  Multiplexer #(.width(16)) multiplexer_11 (
    .in0(register_17_q), .in1(adder_9_out), .out(multiplexer_11_out), .sel(in_55));
  Adder #(.width(16)) adder_9 (.a(16'h1), .b(register_17_q), .out(adder_9_out));  // open: cin, cout
  nand nand_16 (nand_16_out, SR_Flip_Flop, clock_1_out);
  nand nand_17 (nand_17_out, clock_1_out, in_10);
  Clock clock_2 (.out(clock_2_out));
  D_Flip_Flop d_ff_1 (.D(multiplexer_12_out), .clk(clock_3_out), .Q(d_ff_1_q));  // open: Qn, preset, reset
  Multiplexer multiplexer_12 (.in0(d_ff_1_q), .in1(in_24), .out(multiplexer_12_out), .sel(in_25));
  Clock clock_3 (.out(clock_3_out));
  Clock clock_4 (.out(clock_4_out));
  Multiplexer #(.width(16)) multiplexer_13 (
    .in0(multiplexer_11_out), .in1(in_54), .out(multiplexer_13_out), .sel(in_56));
  or or_20 (or_20_out, in_55, in_56);
  nand nand_18 (nand_18_out, nand_16_out, nand_19_out);
  nand nand_19 (nand_19_out, nand_18_out, nand_17_out);
  nand nand_20 (nand_20_out, Data_Flip_Flop, clock_2_out);
  nand nand_21 (nand_21_out, clock_2_out, not_7_out);
  // LedBar #(.inputtype("row"), .matrixcols(16)) ledbar_9: pin names not known; wires that end beside it: multiplexer_12_out, ledbar_9_p2
  Register #(.width(1)) register_1 (.D(in_28[0]), .en(in_29), .clk(clock_4_out), .Q(ledbar_9_p2[0]));  // open: clr
  Register #(.width(1)) register_2 (.D(in_28[1]), .en(in_29), .clk(clock_4_out), .Q(ledbar_9_p2[1]));  // open: clr
  Register #(.width(1)) register_3 (.D(in_28[2]), .en(in_29), .clk(clock_4_out), .Q(ledbar_9_p2[2]));  // open: clr
  Register #(.width(1)) register_4 (.D(in_28[3]), .en(in_29), .clk(clock_4_out), .Q(ledbar_9_p2[3]));  // open: clr
  Register #(.width(1)) register_5 (.D(in_28[4]), .en(in_29), .clk(clock_4_out), .Q(ledbar_9_p2[4]));  // open: clr
  Register #(.width(1)) register_6 (.D(in_28[5]), .en(in_29), .clk(clock_4_out), .Q(ledbar_9_p2[5]));  // open: clr
  Register #(.width(1)) register_7 (.D(in_28[6]), .en(in_29), .clk(clock_4_out), .Q(ledbar_9_p2[6]));  // open: clr
  Register #(.width(1)) register_8 (.D(in_28[7]), .en(in_29), .clk(clock_4_out), .Q(ledbar_9_p2[7]));  // open: clr
  Register #(.width(1)) register_9 (.D(in_28[8]), .en(in_29), .clk(clock_4_out), .Q(ledbar_9_p2[8]));  // open: clr
  Register #(.width(1)) register_10 (.D(in_28[9]), .en(in_29), .clk(clock_4_out), .Q(ledbar_9_p2[9]));  // open: clr
  Register #(.width(1)) register_11 (.D(in_28[10]), .en(in_29), .clk(clock_4_out), .Q(ledbar_9_p2[10]));  // open: clr
  Register #(.width(1)) register_12 (.D(in_28[11]), .en(in_29), .clk(clock_4_out), .Q(ledbar_9_p2[11]));  // open: clr
  Register #(.width(1)) register_13 (.D(in_28[12]), .en(in_29), .clk(clock_4_out), .Q(ledbar_9_p2[12]));  // open: clr
  Register #(.width(1)) register_14 (.D(in_28[13]), .en(in_29), .clk(clock_4_out), .Q(ledbar_9_p2[13]));  // open: clr
  Register #(.width(1)) register_15 (.D(in_28[14]), .en(in_29), .clk(clock_4_out), .Q(ledbar_9_p2[14]));  // open: clr
  Register #(.width(1)) register_16 (.D(in_28[15]), .en(in_29), .clk(clock_4_out), .Q(ledbar_9_p2[15]));  // open: clr
  Register #(.width(16)) register_17 (
    .D(multiplexer_14_out), .en(or_21_out), .clk(clock_5_out), .Q(register_17_q));  // open: clr
  Clock clock_5 (.out(clock_5_out));
  Multiplexer #(.width(16)) multiplexer_14 (
    .in0(multiplexer_13_out), .in1({16{1'b0}}), .out(multiplexer_14_out), .sel(in_57));
  or or_21 (or_21_out, or_20_out, in_57);
  LED led_19 (.in(nand_18_out));
  LED led_20 (.in(nand_19_out));
  nand nand_22 (nand_22_out, nand_20_out, nand_23_out);
  LED led_21 (.in(nand_22_out));
  nand nand_23 (nand_23_out, nand_22_out, nand_21_out);
  LED led_22 (.in(nand_23_out));
  LED led_23 (.in(d_ff_1_q));
  // LedBar #(.inputtype("row"), .matrixcols(16)) ledbar_10: pin names not known; wires that end beside it: register_17_q, ledbar_10_p2
  Hex_Digit_Display hex_digit_display_1 (.value(register_17_q[15:12]));  // open: dp
  Hex_Digit_Display hex_digit_display_2 (.value(register_17_q[11:8]));  // open: dp
  Hex_Digit_Display hex_digit_display_3 (.value(register_17_q[7:4]));  // open: dp
  Hex_Digit_Display hex_digit_display_4 (.value(register_17_q[3:0]));  // open: dp
  Demultiplexer #(.select(3)) demultiplexer_5 (
    .out0(demultiplexer_5_out0), .out1(demultiplexer_5_out1), .out2(demultiplexer_5_out2),
    .out3(demultiplexer_5_out3), .out4(demultiplexer_5_out4), .out5(demultiplexer_5_out5),
    .out6(demultiplexer_5_out6), .out7(demultiplexer_5_out7), .in(in_12), .sel(in_13));
  // LedBar #(.inputtype("row"), .matrixcols(16)) ledbar_11: pin names not known; wires that end beside it: ledbar_11_p1
  Demultiplexer #(.select(3)) demultiplexer_6 (
    .out0(demultiplexer_6_out0), .out1(demultiplexer_6_out1), .out2(demultiplexer_6_out2),
    .out3(demultiplexer_6_out3), .out4(demultiplexer_6_out4), .out5(demultiplexer_6_out5),
    .out6(demultiplexer_6_out6), .out7(demultiplexer_6_out7), .in(in_38), .sel(in_43[5:3]));
  // LedBar #(.inputtype("row"), .matrixcols(16)) ledbar_12: pin names not known; wires that end beside it: ledbar_12_p1
  Clock clock_6 (.out(clock_6_out));
  Register #(.width(16)) register_18 (
    .D(in_6), .en(demultiplexer_5_out0), .clk(clock_6_out), .Q(register_18_q));  // open: clr
  Register #(.width(16)) register_19 (
    .D(in_6), .en(demultiplexer_5_out1), .clk(clock_6_out), .Q(register_19_q));  // open: clr
  Register #(.width(16)) register_20 (
    .D(in_6), .en(demultiplexer_5_out2), .clk(clock_6_out), .Q(register_20_q));  // open: clr
  Register #(.width(16)) register_21 (
    .D(in_6), .en(demultiplexer_5_out3), .clk(clock_6_out), .Q(register_21_q));  // open: clr
  Register #(.width(16)) register_22 (
    .D(in_6), .en(demultiplexer_5_out4), .clk(clock_6_out), .Q(register_22_q));  // open: clr
  Register #(.width(16)) register_23 (
    .D(in_6), .en(demultiplexer_5_out5), .clk(clock_6_out), .Q(register_23_q));  // open: clr
  Register #(.width(16)) register_24 (
    .D(in_6), .en(demultiplexer_5_out6), .clk(clock_6_out), .Q(register_24_q));  // open: clr
  Register #(.width(16)) register_25 (
    .D(in_6), .en(demultiplexer_5_out7), .clk(clock_6_out), .Q(register_25_q));  // open: clr
  Clock clock_7 (.out(clock_7_out));
  RAM #(.addrWidth(3), .dataWidth(16)) ram_1 (
    .addr(in_43[2:0]), .we(demultiplexer_6_out0), .clk(clock_7_out), .din(in_34), .dout(ram_1_dout));  // open: oe
  RAM #(.addrWidth(3), .dataWidth(16)) ram_2 (
    .addr(in_43[2:0]), .we(demultiplexer_6_out1), .clk(clock_7_out), .din(in_34), .dout(ram_2_dout));  // open: oe
  RAM #(.addrWidth(3), .dataWidth(16)) ram_3 (
    .addr(in_43[2:0]), .we(demultiplexer_6_out2), .clk(clock_7_out), .din(in_34), .dout(ram_3_dout));  // open: oe
  RAM #(.addrWidth(3), .dataWidth(16)) ram_4 (
    .addr(in_43[2:0]), .we(demultiplexer_6_out3), .clk(clock_7_out), .din(in_34), .dout(ram_4_dout));  // open: oe
  Multiplexer #(.select(3), .width(16)) multiplexer_15 (
    .in0(register_18_q), .in1(register_19_q), .in2(register_20_q), .in3(register_21_q), .in4(register_22_q),
    .in5(register_23_q), .in6(register_24_q), .in7(register_25_q), .out(ledbar_12_p1), .sel(in_13));
  RAM #(.addrWidth(3), .dataWidth(16)) ram_5 (
    .addr(in_43[2:0]), .we(demultiplexer_6_out4), .clk(clock_7_out), .din(in_34), .dout(ram_5_dout));  // open: oe
  RAM #(.addrWidth(3), .dataWidth(16)) ram_6 (
    .addr(in_43[2:0]), .we(demultiplexer_6_out5), .clk(clock_7_out), .din(in_34), .dout(ram_6_dout));  // open: oe
  RAM #(.addrWidth(3), .dataWidth(16)) ram_7 (
    .addr(in_43[2:0]), .we(demultiplexer_6_out6), .clk(clock_7_out), .din(in_34), .dout(ram_7_dout));  // open: oe
  RAM #(.addrWidth(3), .dataWidth(16)) ram_8 (
    .addr(in_43[2:0]), .we(demultiplexer_6_out7), .clk(clock_7_out), .din(in_34), .dout(ram_8_dout));  // open: oe
  Multiplexer #(.select(3), .width(16)) multiplexer_16 (
    .in0(ram_1_dout), .in1(ram_2_dout), .in2(ram_3_dout), .in3(ram_4_dout), .in4(ram_5_dout),
    .in5(ram_6_dout), .in6(ram_7_dout), .in7(ram_8_dout), .out(ledbar_11_p1), .sel(in_43[5:3]));

  // Notes on the sheet:
  //   AND
  //   NOT
  //   OR
  //   MUX4WAY16
  //   DeMUX4WAY16
  //   Chapter 1 - Inception
  //   XOR
  //   MUX
  //   AND
  //   OR
  //   16-bit ALU
  //   Half Adder
  //   Multibit Adders
  //   Chapter 2 - Elegance
  //   1-Bit Register
  //   16-Bit Register
  //   Program Counter
  //   Chapter 3 - Remember
  //   RAM8
  //   RAM64
endmodule
